# Fritzing sketch Fritzing Bronze Challenge Sketch (saved by Fritzing 1.0.2b)
breadboards: 1

parts:
  S1 = SPST Slide Switch [package="SIP THT"]
  A1 = Arduino UNO R4 WiFi
  M1 = MH Sensor Series 4-pin IR Sensor/Line follower [package=THT]
  M2 = MH Sensor Series 4-pin IR Sensor/Line follower [package=THT]
  HC-SR04_Sensor_1 = HC-SR04 Ultrasonic Distance Sensor
  IC1 = L293D [package=THT]
  M5 = gear-motor-encoder-magnet
  M6 = gear-motor-encoder-magnet
  BAT1 = 6xAA battery  # not connected

nets:
  N1: S1.L1, A1.Pin_8, A1.Pin_27
  N2: S1.COM, A1.Pin_39, M1.pin4, M2.pin4, HC-SR04_Sensor_1.VCC, IC1.+Vmotor, IC1.In_4, IC1.+V
  N3: A1.Pin_9, A1.Pin_48, M1.pin3, M2.pin3, HC-SR04_Sensor_1.GND, IC1.0V
  N4: A1.Pin_35, M2.pin2
  N5: A1.Pin_37, IC1.Enable_1
  N6: A1.Pin_38, IC1.In_1
  N7: A1.Pin_40, HC-SR04_Sensor_1.ECHO
  N8: A1.Pin_41, IC1.In_2
  N9: A1.Pin_44, IC1.In_3
  N10: A1.Pin_45, IC1.Enable_2
  N11: A1.Pin_46, HC-SR04_Sensor_1.TRIG
  N12: A1.Pin_47, M1.pin2
  N13: IC1.Out_1_(_Controlled_by_Enable_1_), M6.pin_2
  N14: IC1.Out_2_(_Controlled_by_Enable_1_), M6.pin_1
  N15: IC1.Out_3_(_Controlled_by_Enable_2_), M5.pin_1
  N16: IC1.Out_4_(_Controlled_by_Enable_2_), M5.pin_2

custom parts:
  SPST Slide Switch: SPST slide switch with inline 100mil spacing through hole connection terminals
  Arduino UNO R4 WiFi: The Arduino UNO R4 WiFi merges the RA4M1 microprocessor from Renesas with the ESP32-S3 from Espressif, creating an all-in-one tool for makers with enhanced processing power and a diverse array of new peripherals.
  MH Sensor Series 4-pin IR Sensor/Line follower: modified version of FC-51 from Peter Van Epp (vanepp in forums) This is the 4-pin version of IR line follower module, using the TCRT5000 sensor and LM393 comparator This one has the analogue output pin, in addition to the Digital pin which is set by the trimmer. The Analog pin can feed an Arduino ADC input, for much better level sensing options and less drift than the crappy potentiometer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
  gear-motor-encoder-magnet: Generic gear motor, 3V to 6V, dual output shafts, 1:48 gear ratio with magnet for wheel encoder
