# Fritzing sketch Lab 3, Pt 1 (saved by Fritzing 1.0.2b)
breadboards: 1

parts:
  M1 = MH Sensor Series 4-pin IR Sensor/Line follower [package=THT]
  A1 = Arduino UNO R4 WiFi
  BAT1 = 6xAA battery  # not connected
  M2 = MH Sensor Series 4-pin IR Sensor/Line follower [package=THT]

nets:
  N1: M1.pin2, A1.Pin_43
  N2: M1.pin3, M1.pin4, A1.Pin_8, A1.Pin_27, M2.pin3, M2.pin4
  N3: A1.Pin_44, M2.pin2

custom parts:
  MH Sensor Series 4-pin IR Sensor/Line follower: modified version of FC-51 from Peter Van Epp (vanepp in forums) This is the 4-pin version of IR line follower module, using the TCRT5000 sensor and LM393 comparator This one has the analogue output pin, in addition to the Digital pin which is set by the trimmer. The Analog pin can feed an Arduino ADC input, for much better level sensing options and less drift than the crappy potentiometer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
  Arduino UNO R4 WiFi: The Arduino UNO R4 WiFi merges the RA4M1 microprocessor from Renesas with the ESP32-S3 from Espressif, creating an all-in-one tool for makers with enhanced processing power and a diverse array of new peripherals.
